// Logisim project Regfile.circ as structural Verilog: 1 circuit, main circuit Register File
module Register_File (
  input  [1:0] Read_register_1,
  input  [1:0] Read_register_2,
  input  [1:0] write_register,
  input  [15:0] write_data,
  input  RegWrite,
  input  clock,
  output [15:0] Reg_0_Value,
  output [15:0] Reg_1_Value,
  output [15:0] Reg_2_Value,
  output [15:0] Reg_3_Value,
  output [15:0] Read_Data_1,
  output [15:0] Read_Data_2
);

  wire WReg1, WReg2, WReg3, WReg4;
  wire [15:0] multiplexer_1_out, multiplexer_2_out, multiplexer_3_out, multiplexer_4_out;

  Demultiplexer #(.select(2), .enable("false")) demultiplexer_1 (
    .out0(WReg1), .out1(WReg2), .out2(WReg3), .out3(WReg4), .in(1'b1), .sel(write_register));
  Multiplexer #(.width(16), .enable("false")) multiplexer_1 (
    .in0(Reg_0_Value), .in1(write_data), .out(multiplexer_1_out), .sel(WReg1));
  Multiplexer #(.width(16), .enable("false")) multiplexer_2 (
    .in0(Reg_1_Value), .in1(write_data), .out(multiplexer_2_out), .sel(WReg2));
  Multiplexer #(.width(16), .enable("false")) multiplexer_3 (
    .in0(Reg_2_Value), .in1(write_data), .out(multiplexer_3_out), .sel(WReg3));
  Multiplexer #(.width(16), .enable("false")) multiplexer_4 (
    .in0(Reg_3_Value), .in1(write_data), .out(multiplexer_4_out), .sel(WReg4));
  Register #(.width(16)) register_1 (.D(multiplexer_1_out), .en(RegWrite), .Q(Reg_0_Value), .clk(clock));  // open: clr
  Register #(.width(16)) register_2 (.D(multiplexer_2_out), .en(RegWrite), .Q(Reg_1_Value), .clk(clock));  // open: clr
  Register #(.width(16)) register_3 (.D(multiplexer_3_out), .en(RegWrite), .Q(Reg_2_Value), .clk(clock));  // open: clr
  Register #(.width(16)) register_4 (.D(multiplexer_4_out), .en(RegWrite), .Q(Reg_3_Value), .clk(clock));  // open: clr
  Multiplexer #(.select(2), .width(16), .enable("false")) multiplexer_5 (
    .in0(Reg_0_Value), .in1(Reg_1_Value), .in2(Reg_2_Value), .in3(Reg_3_Value), .out(Read_Data_1),
    .sel(Read_register_1));
  Multiplexer #(.select(2), .width(16), .enable("false")) multiplexer_6 (
    .in0(Reg_0_Value), .in1(Reg_1_Value), .in2(Reg_2_Value), .in3(Reg_3_Value), .out(Read_Data_2),
    .sel(Read_register_2));

  // Other names for the same wires on the sheet: ReadReg1[1:0] = Read_register_1; ReadReg2[1:0] = Read_register_2;
  //   RReg0[15:0] = Reg_0_Value; RReg1[15:0] = Reg_1_Value; RReg2[15:0] = Reg_2_Value; RReg3[15:0] = Reg_3_Value;
  //   writeData[15:0] = write_data; writeReg[1:0] = write_register

  // Notes on the sheet:
  //   These are INPUTS to the circuit
  //   These are INPUTS to the circuit
  //   DO NOT CHANGE THE LOCATIONS OF THE INPUTS/OUTPUTS! IF YOU DO SO, YOU NEED TO MAKE SURE THE PINS ARE AT THE RIGHT PLACE!
  //   These are OUTPUTS to the circuit
  //   Yet again, the clock is not an actual clock, but an input, one that will be driven from a higher circuit
  //   These are OUTPUTS to the circuit
endmodule
