// Logisim project alu.circ as structural Verilog
module main (
  input  [15:0] X,
  input  [15:0] Y,
  input  [3:0] Switch__S,
  output Signed_Overflow,
  output [15:0] RESULT,
  output Equal
);

  wire addOverflow, sltOut, subOverflow;
  wire [15:0] addOut, subOut;

  equal equal_1 (.in_1(X), .in_2(Y), .out(Equal));
  add add_1 (.in_1(X), .in_2(Y), .out_2(addOverflow), .out(addOut));
  sub sub_1 (.in_1(X), .in_2(Y), .out_2(subOverflow), .out(subOut));
  slt slt_1 (.in_1(X), .in_2(Y), .out(sltOut));
  Multiplexer #(.select(4), .width(16)) multiplexer_1 (
    .out(RESULT), .sel(Switch__S));  // open: in0, in1, in2, in3, in4, in5, in6, in7, in8, in9, in10, in11, in12, in13, in14, in15, en

  // Other names for the same wires on the sheet: Overflow = Signed_Overflow; SelectorBits[3:0] = Switch__S

  // Notes on the sheet:
  //   INPUTS to your circuit
  //   INPUT to your circuit
  //   add
  //   sub
  //   slt
  //   DON'T CHANGE THE INPUTS AND OUTPUTS! IF YOU DO SO, YOU NEED TO MAKE SURE THE PINS ARE IN THE RIGHT PLACES!
  //   OUTPUTS of your circuit
endmodule

module add (
  input  [15:0] in_1,
  input  [15:0] in_2,
  output [15:0] out,
  output out_2
);

  Adder #(.width(16)) adder_1 (.a(in_1), .b(in_2), .out(out), .cout(out_2));  // open: cin
endmodule

module sub (
  input  [15:0] in_1,
  input  [15:0] in_2,
  output [15:0] out,
  output out_2
);

  Subtractor #(.width(16)) subtractor_1 (.a(in_1), .b(in_2), .out(out), .bout(out_2));  // open: bin
endmodule

module slt (
  input  [15:0] in_1,
  input  [15:0] in_2,
  output out
);

  Comparator #(.width(16)) comparator_1 (.a(in_1), .b(in_2), .lt(out));  // open: gt, eq
endmodule

module \or  (
  input  [15:0] in_1,
  input  [15:0] in_2
);
endmodule

module equal (
  input  [15:0] in_1,
  input  [15:0] in_2,
  output out
);

  Comparator #(.width(16)) comparator_1 (.a(in_1), .b(in_2), .eq(out));  // open: gt, lt
endmodule
